# Fritzing sketch Esquema basico 1 (saved by Fritzing 0.9.3b)
circuit board: 3.65416cm x 3.93333cm
breadboards: 2

parts:
  R1 = Resistor [tolerance=±5% resistance=220 package=THT]
  LED1 = LED - 5mm [color="Red (633nm)" package="5 mm [THT]"]
  VCC1 = Battery
  S1 = Pushbutton [package="[THT]"]
  S2 = Pushbutton [package="[THT]"]  # not connected
  VCC2 = Battery  # not connected
  LED2 = LED - 5mm [color="Red (633nm)" package="5 mm [THT]"]  # not connected

nets:
  N1: R1.Pin_0, LED1.anode
  N2: R1.Pin_1, S1.Pin_3, S1.Pin_4
  N3: VCC1.+, S1.Pin_1, S1.Pin_2
